// Logisim project TP.circ as structural Verilog: 6 circuits, main circuit main
module main (
);

  wire clock_1_out, clock_2_out, decodeur_1_imm_reg, decodeur_1_s, gestion_cond_1_exec;
  wire [1:0] decodeur_1_op;
  wire [3:0] alu2_1_nzcv, decodeur_1_cond, decodeur_1_rd, decodeur_1_rot, decodeur_1_rs1, decodeur_1_rs2;
  wire [7:0] decodeur_1_imm;
  wire [31:0] adder_1_out, banc_reg_1_p2, banc_reg_1_p8, banc_reg_1_p9, calculateur_immediat_1_out_3,
       multiplexer_1_out, PC_q, ram_1_dout;

  Register #(.width(32)) PC (.D(adder_1_out), .en(1'b1), .clk(clock_1_out), .Q(PC_q));  // open: clr
  Clock clock_1 (.out(clock_1_out));
  RAM #(.addrWidth(24), .asyncread("true"), .dataWidth(32)) ram_1 (
    .addr(PC_q[25:2]), .oe(1'b1), .dout(ram_1_dout));  // open: we, clk, din
  Adder #(.width(32)) adder_1 (.a(PC_q), .b(32'h4), .out(adder_1_out));  // open: cin, cout
  decodeur decodeur_1 (
    .in_1(ram_1_dout), .Rs2(decodeur_1_rs2), .Rd(decodeur_1_rd), .Rs1(decodeur_1_rs1), .Op(decodeur_1_op),
    .Imm_reg(decodeur_1_imm_reg), .Imm(decodeur_1_imm), .Rot(decodeur_1_rot), .S(decodeur_1_s),
    .Cond(decodeur_1_cond));
  calculateur_immediat calculateur_immediat_1 (
    .Imm(decodeur_1_imm), .Rot(decodeur_1_rot), .out_3(calculateur_immediat_1_out_3));
  gestion_cond gestion_cond_1 (
    .Cond(decodeur_1_cond), .NZCV(alu2_1_nzcv), .MaJ(decodeur_1_s), .Exec(gestion_cond_1_exec));
  Clock clock_2 (.out(clock_2_out));
  // Probe on alu2_1_nzcv
  // banc_reg banc_reg_1: pin names not known; wires that end beside it: clock_2_out, banc_reg_1_p2, decodeur_1_rd, decodeur_1_rs1, decodeur_1_rs2, gestion_cond_1_exec, {{8{1'b0}}, PC_q[23:0]}, banc_reg_1_p8, banc_reg_1_p9
  Multiplexer #(.width(32)) multiplexer_1 (
    .in0(banc_reg_1_p9), .in1(calculateur_immediat_1_out_3), .out(multiplexer_1_out), .sel(decodeur_1_imm_reg));
  ALU2 alu2_1 (
    .Op1(banc_reg_1_p8), .Op2(multiplexer_1_out), .Sel(decodeur_1_op), .Sortie(banc_reg_1_p2),
    .NZCV(alu2_1_nzcv));
endmodule

module decodeur (
  input  [31:0] in_1,
  output [3:0] Rs2,
  output [3:0] Rd,
  output [3:0] Rs1,
  output [1:0] Op,
  output Imm_reg,
  output [7:0] Imm,
  output [3:0] Rot,
  output S,
  output [3:0] Cond
);

  wire and_1_out, and_2_out, not_1_out, not_2_out, not_3_out;

  not not_1 (not_1_out, in_1[23]);
  not not_2 (not_2_out, in_1[21]);
  and and_1 (and_1_out, in_1[24], not_1_out, in_1[22], not_2_out);
  not not_3 (not_3_out, in_1[24]);
  Multiplexer #(.width(4)) multiplexer_1 (.in0(in_1[15:12]), .in1(4'b1111), .out(Rd), .sel(and_1_out));
  and and_2 (and_2_out, in_1[23], not_3_out);
  or or_1 (Op[0], in_1[21], in_1[22]);
  or or_2 (Op[1], in_1[22], and_2_out);

  assign Cond = in_1[31:28];
  assign Imm = in_1[7:0];
  assign Imm_reg = in_1[25];
  assign Rot = in_1[11:8];
  assign Rs1 = in_1[19:16];
  assign Rs2 = in_1[3:0];
  assign S = in_1[20];
endmodule

module calculateur_immediat (
  input  [7:0] Imm,
  input  [3:0] Rot,
  output [31:0] out_3
);

  Shifter #(.shift("rr"), .width(32)) shifter_1 (.in({{25{Imm[7]}}, Imm[6:0]}), .\dist ({Rot, 1'b0}), .out(out_3));
endmodule

module gestion_cond (
  input  [3:0] Cond,
  input  [3:0] NZCV,
  input  MaJ,
  output Exec
);

  wire and_1_out, and_2_out, and_3_out, and_4_out, and_5_out, and_6_out, and_7_out, and_8_out, and_9_out,
       and_10_out, and_11_out, and_12_out, and_13_out, and_14_out, and_15_out, and_16_out, and_17_out,
       and_18_out, and_19_out, and_20_out, and_21_out, and_22_out, clock_1_out, decodeur_cond_1_al,
       decodeur_cond_1_cc_lo, decodeur_cond_1_cs_hs, decodeur_cond_1_eq, decodeur_cond_1_ge,
       decodeur_cond_1_gt, decodeur_cond_1_hi, decodeur_cond_1_le, decodeur_cond_1_ls, decodeur_cond_1_lt,
       decodeur_cond_1_mi, decodeur_cond_1_ne, decodeur_cond_1_pl, decodeur_cond_1_vc, decodeur_cond_1_vs,
       not_1_out, not_2_out, not_3_out, not_4_out, not_5_out, not_6_out, not_7_out, not_8_out, not_9_out,
       not_10_out, not_11_out, not_12_out, not_13_out, not_14_out, not_15_out, or_1_out, or_2_out, or_3_out,
       or_4_out, or_5_out;
  wire [3:0] CPSR_q;

  Clock clock_1 (.out(clock_1_out));
  Register #(.width(4)) CPSR (.D(NZCV), .en(MaJ), .clk(clock_1_out), .Q(CPSR_q));  // open: clr
  decodeur_cond decodeur_cond_1 (
    .Cond(Cond), .EQ(decodeur_cond_1_eq), .NE(decodeur_cond_1_ne), .CS_HS(decodeur_cond_1_cs_hs),
    .CC_LO(decodeur_cond_1_cc_lo), .MI(decodeur_cond_1_mi), .PL(decodeur_cond_1_pl), .VS(decodeur_cond_1_vs),
    .VC(decodeur_cond_1_vc), .HI(decodeur_cond_1_hi), .LS(decodeur_cond_1_ls), .GE(decodeur_cond_1_ge),
    .LT(decodeur_cond_1_lt), .GT(decodeur_cond_1_gt), .LE(decodeur_cond_1_le), .AL(decodeur_cond_1_al));  // open: NV
  and and_1 (and_1_out, decodeur_cond_1_eq, CPSR_q[2]);
  and and_2 (and_2_out, decodeur_cond_1_ne, not_1_out);
  not not_1 (not_1_out, CPSR_q[2]);
  and and_3 (and_3_out, decodeur_cond_1_cs_hs, CPSR_q[1]);
  and and_4 (and_4_out, decodeur_cond_1_cc_lo, not_2_out);
  not not_2 (not_2_out, CPSR_q[1]);
  and and_5 (and_5_out, decodeur_cond_1_mi, CPSR_q[3]);
  and and_6 (and_6_out, decodeur_cond_1_pl, not_3_out);
  not not_3 (not_3_out, CPSR_q[3]);
  and and_7 (and_7_out, decodeur_cond_1_vs, CPSR_q[0]);
  and and_8 (and_8_out, decodeur_cond_1_vc, not_4_out);
  not not_4 (not_4_out, CPSR_q[0]);
  not not_5 (not_5_out, CPSR_q[2]);
  and and_9 (and_9_out, not_5_out, CPSR_q[1], decodeur_cond_1_hi);
  not not_6 (not_6_out, CPSR_q[1]);
  or or_1 (or_1_out, not_6_out, CPSR_q[2]);
  and and_10 (and_10_out, CPSR_q[3], CPSR_q[3]);
  not not_7 (not_7_out, CPSR_q[0]);
  and and_11 (and_11_out, not_7_out, not_8_out);
  not not_8 (not_8_out, CPSR_q[0]);
  and and_12 (and_12_out, CPSR_q[3], not_9_out);
  not not_9 (not_9_out, CPSR_q[0]);
  not not_10 (not_10_out, CPSR_q[3]);
  and and_13 (and_13_out, not_10_out, CPSR_q[0]);
  not not_11 (not_11_out, CPSR_q[2]);
  and and_14 (and_14_out, not_11_out, CPSR_q[3], CPSR_q[0]);
  not not_12 (not_12_out, CPSR_q[3]);
  and and_15 (and_15_out, not_12_out, not_13_out);
  not not_13 (not_13_out, CPSR_q[0]);
  and and_16 (and_16_out, CPSR_q[3], not_14_out);
  not not_14 (not_14_out, CPSR_q[0]);
  not not_15 (not_15_out, CPSR_q[3]);
  and and_17 (and_17_out, not_15_out, CPSR_q[0]);
  and and_18 (and_18_out, or_1_out, decodeur_cond_1_ls);
  or or_2 (or_2_out, and_10_out, and_11_out);
  or or_3 (or_3_out, and_12_out, and_13_out);
  or or_4 (or_4_out, and_14_out, and_15_out);
  or or_5 (or_5_out, CPSR_q[3], and_16_out, and_17_out);
  and and_19 (and_19_out, or_2_out, decodeur_cond_1_ge);
  and and_20 (and_20_out, or_3_out, decodeur_cond_1_lt);
  and and_21 (and_21_out, or_4_out, decodeur_cond_1_gt);
  and and_22 (and_22_out, or_5_out, decodeur_cond_1_le);
  or or_6 (Exec, and_1_out, and_2_out, and_3_out, and_4_out, and_5_out, and_6_out, and_7_out, and_8_out, and_9_out, and_18_out, and_19_out, and_20_out, and_21_out, and_22_out, decodeur_cond_1_al);
endmodule

module decodeur_cond (
  input  [3:0] Cond,
  output EQ,
  output NE,
  output CS_HS,
  output CC_LO,
  output MI,
  output PL,
  output VS,
  output VC,
  output HI,
  output LS,
  output GE,
  output LT,
  output GT,
  output LE,
  output AL,
  output NV
);

  Decoder #(.select(4)) decoder_1 (
    .out0(EQ), .out1(NE), .out2(CS_HS), .out3(CC_LO), .out4(MI), .out5(PL), .out6(VS), .out7(VC), .out8(HI),
    .out9(LS), .out10(GE), .out11(LT), .out12(GT), .out13(LE), .out14(AL), .out15(NV), .sel(Cond));  // open: en
endmodule

module ALU2 (
  input  [31:0] Op1,
  input  [31:0] Op2,
  input  [1:0] Sel,
  output [31:0] Sortie,
  output [3:0] NZCV
);

  wire adder_1_cout, and_1_out, multiplexer_1_out, not_1_out, not_2_out, or_1_out, subtractor_1_bout,
       xor_1_out, xor_2_out;
  wire [31:0] adder_1_out, and_3_out, subtractor_1_out;

  ExactlyOne xor_1 (.out(xor_1_out), .in0(Sel[0]), .in1(Op2[31]), .in2(Op1[31]));
  not not_1 (not_1_out, xor_1_out);
  and and_1 (and_1_out, not_1_out, xor_2_out);
  and and_2 (NZCV[0], Sel[1], and_1_out);
  xor xor_2 (xor_2_out, Op1[31], NZCV[3]);
  assign and_3_out = Op1 & Op2;  // AND_Gate and_3, 32 bits wide
  Adder #(.width(32)) adder_1 (.a(Op1), .b(Op2), .out(adder_1_out), .cout(adder_1_cout));  // open: cin
  Subtractor #(.width(32)) subtractor_1 (
    .a(Op1), .b(Op2), .out(subtractor_1_out), .bout(subtractor_1_bout));  // open: bin
  Multiplexer multiplexer_1 (.in0(adder_1_cout), .in1(not_2_out), .out(multiplexer_1_out), .sel(Sel[0]));
  not not_2 (not_2_out, subtractor_1_bout);
  Multiplexer multiplexer_2 (.in0(1'b0), .in1(multiplexer_1_out), .out(NZCV[1]), .sel(Sel[1]));
  Multiplexer #(.select(2), .width(32)) multiplexer_3 (
    .in0(and_3_out), .in1(Op2), .in2(adder_1_out), .in3(subtractor_1_out), .out({NZCV[3], Sortie[30:0]}),
    .sel(Sel));
  or or_1 (or_1_out, NZCV[3], Sortie[30], Sortie[29], Sortie[28], Sortie[27], Sortie[26], Sortie[25], Sortie[24], Sortie[23], Sortie[22], Sortie[21], Sortie[20], Sortie[19], Sortie[18], Sortie[17], Sortie[16], Sortie[15], Sortie[14], Sortie[13], Sortie[11], Sortie[10], Sortie[9], Sortie[8], Sortie[7], Sortie[6], Sortie[5], Sortie[4], Sortie[3], Sortie[2], Sortie[1], Sortie[0], Sortie[12]);
  not not_3 (NZCV[2], or_1_out);

  assign Sortie[31] = NZCV[3];
endmodule
